# Fritzing sketch Layout (saved by Fritzing 0.9.3b)
circuit board: 8.46667cm x 5.64444cm
breadboards: 1

parts:
  RFID_Reader = RFID-RC522-v3
  DFRobot_DFPlayer_Mini = DFRobot DFPlayer Mini [part_number=DFR0299]
  Down = Round Pushbutton
  Pause = Round Pushbutton
  Up = Round Pushbutton
  U1 = lolin
  R1 = Resistor [tolerance=±5% resistance=1k package="0402 [SMD]"]

nets:
  N1: RFID_Reader.SDA, U1.connector32
  N2: RFID_Reader.SCK, U1.connector27
  N3: RFID_Reader.MOSI, U1.connector28
  N4: RFID_Reader.MISO, U1.connector29
  N5: RFID_Reader.RST, DFRobot_DFPlayer_Mini.GND-1, DFRobot_DFPlayer_Mini.GND-2, U1.connector33
  3.3V: RFID_Reader.3.3V, DFRobot_DFPlayer_Mini.VCC, U1.connector0, U1.connector34
  N6: DFRobot_DFPlayer_Mini.RX, U1.connector24, R1.Pin_0, R1.Pin_1
  N7: DFRobot_DFPlayer_Mini.TX, U1.connector23
  N8: DFRobot_DFPlayer_Mini.BUSY, U1.connector22
  N9: Down.leg0, Pause.leg0, Up.leg0, U1.connector15, U1.connector17, U1.connector20, U1.connector37
  N10: Down.leg1, U1.connector10
  N11: Pause.leg1, U1.connector8
  N12: Up.leg1, U1.connector9

custom parts:
  RFID-RC522-v3: A simple China made RFID-RC522 Reader (6x4 cm); do check the pin labels, as this is a MFRC522 based clone.
